# Fritzing sketch vent_control_ambientika (saved by Fritzing 1.0.4)
breadboards: 1

parts:
  Mod1 = Amica NodeMCU DEVKIT 1.0
  R2 = Resistor [tolerance=±5% power=0.25W resistance=10K package=THT]
  part = Basic FET N-Channel [part_number=IRLZ44N package="TO220 [THT]"]
  D1 = Schottky Diode [part_number=1N5817 package="300 mil [THT]"]
  R1 = Resistor [tolerance=±5% power=0.25W resistance=10K package=THT]
  R4 = Resistor [tolerance=±5% power=0.25W resistance=10K package=THT]
  part_2 = mystery part, 8 pins [chip_label=MP1584EN part_number=MP1584EN]

nets:
  N1: Mod1.pin2, Mod1.pin_9, Mod1.pin_29, R2.Pin_1, part.source, R4.Pin_1, part_2.pin4, part_2.pin5
  N2: Mod1.pin6, part.gate, R4.Pin_0
  N3: Mod1.pin_30, part_2.pin8
  N4: R2.Pin_0, part.drain, D1.anode, R1.Pin_0
  N5: D1.cathode, R1.Pin_1, part_2.pin1

notes:
  5V
  24V
  VENT
